// Logisim project branch-comp.circ as structural Verilog: 1 circuit, main circuit branch_comp
module branch_comp (
  input  [31:0] BrData1,
  input  [31:0] BrData2,
  input  BrUn,
  output BrEq,
  output BrLt
);

  wire S_EQ, S_LT, U_EQ, U_LT;

  Comparator #(.mode("unsigned"), .width(32)) comparator_1 (
    .a(BrData1), .b(BrData2), .eq(U_EQ), .lt(U_LT));  // open: gt
  Comparator #(.width(32)) comparator_2 (.a(BrData1), .b(BrData2), .eq(S_EQ), .lt(S_LT));  // open: gt
  Multiplexer multiplexer_1 (.in0(S_EQ), .in1(U_EQ), .out(BrEq), .sel(BrUn));
  Multiplexer multiplexer_2 (.in0(S_LT), .in1(U_LT), .out(BrLt), .sel(BrUn));

  // Notes on the sheet:
  //   INPUTS to your circuit
  //   Unsigned
  //   Signed
  //   DON'T CHANGE THE LOCATIONS OF THE INPUTS AND OUTPUTS!
  //   OUTPUT from your circuit
endmodule
