// Logisim project control-logic.circ as structural Verilog: 1 circuit, main circuit control_logic
module control_logic (
  input  [31:0] Instruction,
  input  BrEq,
  input  BrLt,
  output PCSel,
  output RegWEn,
  output [2:0] ImmSel,
  output BrUn,
  output ASel,
  output BSel,
  output [3:0] ALUSel,
  output MemWEn,
  output [1:0] WBSel
);

  wire and_2_out, and_5_out, and_6_out, and_9_out, and_10_out, and_11_out, and_12_out, and_13_out,
       and_14_out, and_15_out, and_16_out, and_17_out, and_18_out, and_19_out, and_20_out, and_49_out,
       and_50_out, and_51_out, and_52_out, comparator_2_eq, comparator_3_eq, comparator_4_eq,
       comparator_5_eq, comparator_6_eq, comparator_7_eq, comparator_8_eq, comparator_9_eq, comparator_11_eq,
       comparator_12_eq, comparator_13_eq, comparator_14_eq, comparator_15_eq, comparator_16_eq,
       comparator_17_eq, comparator_18_eq, comparator_19_eq, comparator_20_eq, comparator_21_eq,
       comparator_22_eq, comparator_24_eq, comparator_25_eq, comparator_28_eq, comparator_29_eq,
       comparator_30_eq, comparator_31_eq, comparator_32_eq, comparator_33_eq, comparator_34_eq,
       comparator_35_eq, comparator_36_eq, comparator_37_eq, comparator_38_eq, comparator_39_eq,
       comparator_40_eq, comparator_41_eq, comparator_42_eq, comparator_43_eq, comparator_44_eq,
       comparator_45_eq, comparator_46_eq, comparator_47_eq, comparator_48_eq, comparator_49_eq,
       comparator_50_eq, comparator_51_eq, comparator_52_eq, comparator_53_eq, comparator_54_eq,
       comparator_55_eq, comparator_56_eq, comparator_57_eq, comparator_58_eq, comparator_59_eq,
       comparator_60_eq, Is_add, Is_addi, Is_and, Is_andi, Is_auipc, Is_beq, Is_bge, Is_bgeu, Is_blt,
       Is_bltu, Is_bne, Is_I_Imm, Is_jal, Is_jalr, Is_lb, Is_lh, Is_lui, Is_lw, Is_mul, Is_mulh, Is_mulhu,
       Is_or, Is_ori, Is_R, Is_SB, Is_sb_t, Is_sh, Is_sll, Is_slli, Is_slt, Is_slti, Is_sra, Is_srai, Is_srl,
       Is_srli, Is_sub, Is_sw, Is_xor, Is_xori, not_1_out, not_2_out, or_1_out, or_2_out, or_3_out;
  wire [5:0] INPUT_ROM;
  wire [15:14] rom_1_data;

  Comparator #(.mode("unsigned"), .width(7)) comparator_1 (
    .a(7'b0010011), .b(Instruction[6:0]), .eq(Is_I_Imm));  // open: gt, lt
  Comparator #(.mode("unsigned"), .width(3)) comparator_2 (
    .a(Instruction[14:12]), .b(3'b000), .eq(comparator_2_eq));  // open: gt, lt
  Comparator #(.mode("unsigned"), .width(3)) comparator_3 (
    .a(Instruction[14:12]), .b(3'b001), .eq(comparator_3_eq));  // open: gt, lt
  Comparator #(.mode("unsigned"), .width(3)) comparator_4 (
    .a(Instruction[14:12]), .b(3'b010), .eq(comparator_4_eq));  // open: gt, lt
  Comparator #(.mode("unsigned"), .width(3)) comparator_5 (
    .a(Instruction[14:12]), .b(3'b100), .eq(comparator_5_eq));  // open: gt, lt
  Comparator #(.mode("unsigned"), .width(3)) comparator_6 (
    .a(Instruction[14:12]), .b(3'b101), .eq(comparator_6_eq));  // open: gt, lt
  Comparator #(.mode("unsigned"), .width(3)) comparator_7 (
    .a(Instruction[14:12]), .b(3'b101), .eq(comparator_7_eq));  // open: gt, lt
  Comparator #(.mode("unsigned"), .width(3)) comparator_8 (
    .a(Instruction[14:12]), .b(3'b110), .eq(comparator_8_eq));  // open: gt, lt
  Comparator #(.mode("unsigned"), .width(3)) comparator_9 (
    .a(Instruction[14:12]), .b(3'b111), .eq(comparator_9_eq));  // open: gt, lt
  Comparator #(.mode("unsigned"), .width(7)) comparator_10 (
    .a(7'b0110011), .b(Instruction[6:0]), .eq(Is_R));  // open: gt, lt
  Comparator #(.mode("unsigned"), .width(3)) comparator_11 (
    .a(Instruction[14:12]), .b(3'b000), .eq(comparator_11_eq));  // open: gt, lt
  Comparator #(.mode("unsigned"), .width(3)) comparator_12 (
    .a(Instruction[14:12]), .b(3'b000), .eq(comparator_12_eq));  // open: gt, lt
  Comparator #(.mode("unsigned"), .width(3)) comparator_13 (
    .a(Instruction[14:12]), .b(3'b000), .eq(comparator_13_eq));  // open: gt, lt
  Comparator #(.mode("unsigned"), .width(3)) comparator_14 (
    .a(Instruction[14:12]), .b(3'b001), .eq(comparator_14_eq));  // open: gt, lt
  Comparator #(.mode("unsigned"), .width(3)) comparator_15 (
    .a(Instruction[14:12]), .b(3'b001), .eq(comparator_15_eq));  // open: gt, lt
  Comparator #(.mode("unsigned"), .width(3)) comparator_16 (
    .a(Instruction[14:12]), .b(3'b011), .eq(comparator_16_eq));  // open: gt, lt
  Comparator #(.mode("unsigned"), .width(3)) comparator_17 (
    .a(Instruction[14:12]), .b(3'b010), .eq(comparator_17_eq));  // open: gt, lt
  Comparator #(.mode("unsigned"), .width(3)) comparator_18 (
    .a(Instruction[14:12]), .b(3'b100), .eq(comparator_18_eq));  // open: gt, lt
  Comparator #(.mode("unsigned"), .width(3)) comparator_19 (
    .a(Instruction[14:12]), .b(3'b101), .eq(comparator_19_eq));  // open: gt, lt
  Comparator #(.mode("unsigned"), .width(3)) comparator_20 (
    .a(Instruction[14:12]), .b(3'b101), .eq(comparator_20_eq));  // open: gt, lt
  Comparator #(.mode("unsigned"), .width(3)) comparator_21 (
    .a(Instruction[14:12]), .b(3'b110), .eq(comparator_21_eq));  // open: gt, lt
  Comparator #(.mode("unsigned"), .width(3)) comparator_22 (
    .a(Instruction[14:12]), .b(3'b111), .eq(comparator_22_eq));  // open: gt, lt
  Comparator #(.mode("unsigned"), .width(7)) comparator_23 (
    .a(7'b1100011), .b(Instruction[6:0]), .eq(Is_SB));  // open: gt, lt
  Comparator #(.width(3)) comparator_24 (.a(Instruction[14:12]), .b(3'b000), .eq(comparator_24_eq));  // open: gt, lt
  Comparator #(.width(7)) comparator_25 (.a(Instruction[6:0]), .b(7'b1100111), .eq(comparator_25_eq));  // open: gt, lt
  Comparator #(.width(7)) comparator_26 (.a(Instruction[6:0]), .b(7'b0010111), .eq(Is_auipc));  // open: gt, lt
  Comparator #(.width(7)) comparator_27 (.a(Instruction[6:0]), .b(7'b0110111), .eq(Is_lui));  // open: gt, lt
  Comparator #(.width(3)) comparator_28 (.a(Instruction[14:12]), .b(3'b000), .eq(comparator_28_eq));  // open: gt, lt
  Comparator #(.width(7)) comparator_29 (.a(Instruction[6:0]), .b(7'b0000011), .eq(comparator_29_eq));  // open: gt, lt
  Comparator #(.width(3)) comparator_30 (.a(Instruction[14:12]), .b(3'b001), .eq(comparator_30_eq));  // open: gt, lt
  Comparator #(.width(7)) comparator_31 (.a(Instruction[6:0]), .b(7'b0000011), .eq(comparator_31_eq));  // open: gt, lt
  Comparator #(.width(3)) comparator_32 (.a(Instruction[14:12]), .b(3'b010), .eq(comparator_32_eq));  // open: gt, lt
  Comparator #(.width(7)) comparator_33 (.a(Instruction[6:0]), .b(7'b0000011), .eq(comparator_33_eq));  // open: gt, lt
  Comparator #(.width(3)) comparator_34 (.a(Instruction[14:12]), .b(3'b000), .eq(comparator_34_eq));  // open: gt, lt
  Comparator #(.width(7)) comparator_35 (.a(Instruction[6:0]), .b(7'b0100011), .eq(comparator_35_eq));  // open: gt, lt
  Comparator #(.width(3)) comparator_36 (.a(Instruction[14:12]), .b(3'b001), .eq(comparator_36_eq));  // open: gt, lt
  Comparator #(.width(7)) comparator_37 (.a(Instruction[6:0]), .b(7'b0100011), .eq(comparator_37_eq));  // open: gt, lt
  Comparator #(.width(3)) comparator_38 (.a(Instruction[14:12]), .b(3'b010), .eq(comparator_38_eq));  // open: gt, lt
  Comparator #(.width(7)) comparator_39 (.a(Instruction[6:0]), .b(7'b0100011), .eq(comparator_39_eq));  // open: gt, lt
  and and_1 (Is_addi, comparator_2_eq, Is_I_Imm);
  and and_2 (and_2_out, comparator_3_eq, Is_I_Imm);
  Comparator #(.mode("unsigned"), .width(7)) comparator_40 (
    .a(Instruction[31:25]), .b({7{1'b0}}), .eq(comparator_40_eq));  // open: gt, lt
  and and_3 (Is_slti, comparator_4_eq, Is_I_Imm);
  and and_4 (Is_xori, comparator_5_eq, Is_I_Imm);
  and and_5 (and_5_out, comparator_6_eq, Is_I_Imm);
  Comparator #(.mode("unsigned"), .width(7)) comparator_41 (
    .a(Instruction[31:25]), .b({7{1'b0}}), .eq(comparator_41_eq));  // open: gt, lt
  and and_6 (and_6_out, comparator_7_eq, Is_I_Imm);
  Comparator #(.mode("unsigned"), .width(7)) comparator_42 (
    .a(Instruction[31:25]), .b(7'b0100000), .eq(comparator_42_eq));  // open: gt, lt
  and and_7 (Is_ori, comparator_8_eq, Is_I_Imm);
  and and_8 (Is_andi, comparator_9_eq, Is_I_Imm);
  and and_9 (and_9_out, comparator_11_eq, Is_R);
  Comparator #(.mode("unsigned"), .width(7)) comparator_43 (
    .a(Instruction[31:25]), .b({7{1'b0}}), .eq(comparator_43_eq));  // open: gt, lt
  and and_10 (and_10_out, comparator_12_eq, Is_R);
  Comparator #(.mode("unsigned"), .width(7)) comparator_44 (
    .a(Instruction[31:25]), .b(7'b0000001), .eq(comparator_44_eq));  // open: gt, lt
  and and_11 (and_11_out, comparator_13_eq, Is_R);
  Comparator #(.mode("unsigned"), .width(7)) comparator_45 (
    .a(Instruction[31:25]), .b(7'b0100000), .eq(comparator_45_eq));  // open: gt, lt
  and and_12 (and_12_out, comparator_14_eq, Is_R);
  Comparator #(.mode("unsigned"), .width(7)) comparator_46 (
    .a(Instruction[31:25]), .b({7{1'b0}}), .eq(comparator_46_eq));  // open: gt, lt
  and and_13 (and_13_out, comparator_15_eq, Is_R);
  Comparator #(.mode("unsigned"), .width(7)) comparator_47 (
    .a(Instruction[31:25]), .b(7'b0000001), .eq(comparator_47_eq));  // open: gt, lt
  and and_14 (and_14_out, comparator_16_eq, Is_R);
  Comparator #(.mode("unsigned"), .width(7)) comparator_48 (
    .a(Instruction[31:25]), .b(7'b0000001), .eq(comparator_48_eq));  // open: gt, lt
  and and_15 (and_15_out, comparator_17_eq, Is_R);
  Comparator #(.mode("unsigned"), .width(7)) comparator_49 (
    .a(Instruction[31:25]), .b({7{1'b0}}), .eq(comparator_49_eq));  // open: gt, lt
  and and_16 (and_16_out, comparator_18_eq, Is_R);
  Comparator #(.mode("unsigned"), .width(7)) comparator_50 (
    .a(Instruction[31:25]), .b({7{1'b0}}), .eq(comparator_50_eq));  // open: gt, lt
  and and_17 (and_17_out, comparator_19_eq, Is_R);
  Comparator #(.mode("unsigned"), .width(7)) comparator_51 (
    .a(Instruction[31:25]), .b({7{1'b0}}), .eq(comparator_51_eq));  // open: gt, lt
  and and_18 (and_18_out, comparator_20_eq, Is_R);
  Comparator #(.mode("unsigned"), .width(7)) comparator_52 (
    .a(Instruction[31:25]), .b(7'b0100000), .eq(comparator_52_eq));  // open: gt, lt
  and and_19 (and_19_out, comparator_21_eq, Is_R);
  Comparator #(.mode("unsigned"), .width(7)) comparator_53 (
    .a(Instruction[31:25]), .b({7{1'b0}}), .eq(comparator_53_eq));  // open: gt, lt
  and and_20 (and_20_out, comparator_22_eq, Is_R);
  Comparator #(.mode("unsigned"), .width(7)) comparator_54 (
    .a(Instruction[31:25]), .b({7{1'b0}}), .eq(comparator_54_eq));  // open: gt, lt
  Comparator #(.mode("unsigned"), .width(3)) comparator_55 (
    .a(Instruction[14:12]), .b(3'b000), .eq(comparator_55_eq));  // open: gt, lt
  and and_21 (Is_beq, comparator_55_eq, Is_SB);
  Comparator #(.mode("unsigned"), .width(3)) comparator_56 (
    .a(Instruction[14:12]), .b(3'b001), .eq(comparator_56_eq));  // open: gt, lt
  and and_22 (Is_bne, comparator_56_eq, Is_SB);
  Comparator #(.mode("unsigned"), .width(3)) comparator_57 (
    .a(Instruction[14:12]), .b(3'b100), .eq(comparator_57_eq));  // open: gt, lt
  and and_23 (Is_blt, comparator_57_eq, Is_SB);
  Comparator #(.mode("unsigned"), .width(3)) comparator_58 (
    .a(Instruction[14:12]), .b(3'b101), .eq(comparator_58_eq));  // open: gt, lt
  and and_24 (Is_bge, comparator_58_eq, Is_SB);
  Comparator #(.mode("unsigned"), .width(3)) comparator_59 (
    .a(Instruction[14:12]), .b(3'b110), .eq(comparator_59_eq));  // open: gt, lt
  and and_25 (Is_bltu, comparator_59_eq, Is_SB);
  Comparator #(.mode("unsigned"), .width(3)) comparator_60 (
    .a(Instruction[14:12]), .b(3'b111), .eq(comparator_60_eq));  // open: gt, lt
  and and_26 (Is_bgeu, comparator_60_eq, Is_SB);
  Comparator #(.width(7)) comparator_61 (.a(Instruction[6:0]), .b(7'b1101111), .eq(Is_jal));  // open: gt, lt
  and and_27 (Is_jalr, comparator_24_eq, comparator_25_eq);
  and and_28 (Is_lb, comparator_28_eq, comparator_29_eq);
  and and_29 (Is_lh, comparator_30_eq, comparator_31_eq);
  and and_30 (Is_lw, comparator_32_eq, comparator_33_eq);
  and and_31 (Is_sb_t, comparator_34_eq, comparator_35_eq);
  and and_32 (Is_sh, comparator_36_eq, comparator_37_eq);
  and and_33 (Is_sw, comparator_38_eq, comparator_39_eq);
  and and_34 (Is_slli, and_2_out, comparator_40_eq);
  and and_35 (Is_srli, and_5_out, comparator_41_eq);
  and and_36 (Is_srai, and_6_out, comparator_42_eq);
  and and_37 (Is_add, and_9_out, comparator_43_eq);
  and and_38 (Is_mul, and_10_out, comparator_44_eq);
  and and_39 (Is_sub, and_11_out, comparator_45_eq);
  and and_40 (Is_sll, and_12_out, comparator_46_eq);
  and and_41 (Is_mulh, and_13_out, comparator_47_eq);
  and and_42 (Is_mulhu, and_14_out, comparator_48_eq);
  and and_43 (Is_slt, and_15_out, comparator_49_eq);
  and and_44 (Is_xor, and_16_out, comparator_50_eq);
  and and_45 (Is_srl, and_17_out, comparator_51_eq);
  and and_46 (Is_sra, and_18_out, comparator_52_eq);
  and and_47 (Is_or, and_19_out, comparator_53_eq);
  and and_48 (Is_and, and_20_out, comparator_54_eq);
  ROM #(.addrWidth(6), .dataWidth(16)) rom_1 (
    .addr(INPUT_ROM), .data({rom_1_data, WBSel, MemWEn, ALUSel, BSel, ASel, BrUn, ImmSel, RegWEn}));
  Priority_Encoder #(.select_enc(6)) priority_encoder_1 (
    .in0(Is_add), .in1(Is_mul), .in2(Is_sub), .in3(Is_sll), .in4(Is_mulh), .in5(Is_mulhu), .in6(Is_slt),
    .in7(Is_xor), .in8(Is_srl), .in9(Is_sra), .in10(Is_or), .in11(Is_and), .in12(Is_lb), .in13(Is_lh),
    .in14(Is_lw), .in15(Is_addi), .in16(Is_slli), .in17(Is_slti), .in18(Is_xori), .in19(Is_srli),
    .in20(Is_srai), .in21(Is_ori), .in22(Is_andi), .in23(Is_sb_t), .in24(Is_sh), .in25(Is_sw), .in26(Is_beq),
    .in27(Is_bne), .in28(Is_blt), .in29(Is_bge), .in30(Is_bltu), .in31(Is_bgeu), .in32(Is_auipc),
    .in33(Is_lui), .in34(Is_jal), .in35(Is_jalr), .out(INPUT_ROM));  // open: in36, in37, in38, in39, in40, in41, in42, in43, in44, in45, in46, in47, in48, in49, in50, in51, in52, in53, in54, in55, in56, in57, in58, in59, in60, in61, in62, in63, gs, en_out, en_in
  not not_1 (not_1_out, BrLt);
  or or_1 (or_1_out, Is_bge, Is_bgeu);
  not not_2 (not_2_out, BrEq);
  or or_2 (or_2_out, Is_blt, Is_bltu);
  or or_3 (or_3_out, Is_jal, Is_jalr);
  and and_49 (and_49_out, not_1_out, or_1_out);
  and and_50 (and_50_out, BrEq, Is_beq);
  and and_51 (and_51_out, Is_bne, not_2_out);
  and and_52 (and_52_out, or_2_out, BrLt);
  or or_4 (PCSel, or_3_out, and_49_out, and_50_out, and_51_out, and_52_out);

  // Other names for the same wires on the sheet: Opcode[6:0] = Instruction[6:0]; Ins_7_32[24:0] = Instruction[31:7];
  //   I_Imm_Funct3[2:0] = Instruction[14:12]; I_Imm_Funct7[6:0] = Instruction[31:25]

  // Notes on the sheet:
  //   INPUTS to your circuit
  //   DON'T CHANGE THE LOCATIONS OF THE INPUTS AND OUTPUTS!
  //   OUTPUT from your circuit
  //   contents of rom_1 (hex, n*v repeats v):
  //   1001 1401 1601 1081 1481 1581 1101 1201 1281 1681 1301 1381 41 41 41 1041 10c1 1141 1241 12c1 16c1
  //   1341 13c1 842 842 842 4*64 74 74 1067 17c7 2069 2041
  //   ROM FOR CONTROL LOGIC
  //   This is only if you choose to do the ROM option
  //   Reminder: If using ROM, use combinational logic for PCSel
endmodule
