// Logisim project imm-gen.circ as structural Verilog: 1 circuit, main circuit imm_gen
module imm_gen (
  input  [31:0] Instruction,
  input  [2:0] ImmSel,
  output [31:0] Immediate
);

  wire [31:0] B_Immediate, I_Immediate, J_Immediate, S_Immediate;

  assign I_Immediate = {{20{Instruction[31]}}, Instruction[31:20]};  // Bit_Extender bit_extender_1
  assign J_Immediate = {{11{Instruction[31]}}, {Instruction[31], Instruction[19:12], Instruction[20], Instruction[30:21], 1'b0}};  // Bit_Extender bit_extender_2
  assign B_Immediate = {{19{Instruction[31]}}, {Instruction[31], Instruction[11], Instruction[30:25], Instruction[10:7], 1'b0}};  // Bit_Extender bit_extender_3
  assign S_Immediate = {{20{Instruction[31]}}, {Instruction[31:25], Instruction[11:7]}};  // Bit_Extender bit_extender_4
  Multiplexer #(.select(3), .width(32)) multiplexer_1 (
    .in0(I_Immediate), .in1(S_Immediate), .in2(B_Immediate), .in3({Instruction[31:12], {12{1'b0}}}),
    .in4(J_Immediate), .out(Immediate), .sel(ImmSel));  // open: in5, in6, in7

  // Other names for the same wires on the sheet: J_1_10[9:0] = Instruction[30:21];
  //   U_Immediate[31:12] = Instruction[31:12]; B_5_10[5:0] = Instruction[30:25]; S_5_10[5:0] = Instruction[30:25];
  //   J_11 = Instruction[20]; J_12_19[7:0] = Instruction[19:12]; B_12 = Instruction[31]; J_20 = Instruction[31];
  //   S_11 = Instruction[31]; B_1_4[3:0] = Instruction[10:7]; S_0_4[4:0] = Instruction[11:7]; B_11 = Instruction[11]

  // Notes on the sheet:
  //   INPUTS to your circuit
  //   DON'T CHANGE THE LOCATIONS OF THE INPUTS AND OUTPUTS!
  //   OUTPUT from your circuit
endmodule
