// Logisim project partial-load.circ as structural Verilog: 1 circuit, main circuit partial_load
module partial_load (
  input  [31:0] Instruction,
  input  [31:0] MemAddress,
  input  [31:0] DataFromMem,
  output [31:0] DataToReg
);

  wire comparator_2_eq, comparator_3_eq, comparator_4_eq, comparator_5_eq, comparator_8_eq, comparator_8_lt,
       comparator_11_eq, comparator_14_eq, comparator_14_lt, comparator_17_eq, comparator_20_eq,
       comparator_20_lt, Is_lb, Is_lh, Is_lw, isLb, isLh, isLoad, isLw;
  wire [2:0] I_Imm_Funct3;
  wire [7:0] multiplexer_1_out;
  wire [15:0] multiplexer_2_out;
  wire [31:0] ByteFromMemData, HalfWordFromMemData;

  Comparator #(.mode("unsigned"), .width(7)) comparator_1 (
    .a(Instruction[6:0]), .b(7'b0000011), .eq(isLoad));  // open: gt, lt
  Comparator #(.mode("unsigned"), .width(3)) comparator_2 (
    .a(Instruction[14:12]), .b(3'b000), .eq(comparator_2_eq));  // open: gt, lt
  Comparator #(.mode("unsigned"), .width(3)) comparator_3 (
    .a(Instruction[14:12]), .b(3'b001), .eq(comparator_3_eq));  // open: gt, lt
  Comparator #(.mode("unsigned"), .width(3)) comparator_4 (
    .a(Instruction[14:12]), .b(3'b010), .eq(comparator_4_eq));  // open: gt, lt
  and and_1 (isLb, comparator_2_eq, isLoad);
  and and_2 (isLh, comparator_3_eq, isLoad);
  and and_3 (isLw, comparator_4_eq, isLoad);
  Comparator #(.width(3)) comparator_5 (
    .a(I_Imm_Funct3), .b(3'b000), .eq(comparator_5_eq), .lt(comparator_5_eq));  // open: gt
  Comparator #(.width(3)) comparator_6 (.a(I_Imm_Funct3), .b(3'b000), .eq(comparator_5_eq));  // open: gt, lt
  Comparator #(.width(3)) comparator_7 (
    .a(I_Imm_Funct3), .b(3'b000), .gt(comparator_5_eq), .eq(comparator_5_eq), .lt(comparator_5_eq));
  Comparator #(.width(7)) comparator_8 (
    .a(Instruction[6:0]), .b(7'b0000011), .eq(comparator_8_eq), .lt(comparator_8_lt));  // open: gt
  Comparator #(.width(7)) comparator_9 (.a(Instruction[6:0]), .b(7'b0000011), .eq(comparator_8_lt));  // open: gt, lt
  Comparator #(.width(7)) comparator_10 (
    .a(Instruction[6:0]), .b(7'b0000011), .gt(comparator_8_eq), .eq(comparator_8_lt));  // open: lt
  Comparator #(.width(3)) comparator_11 (
    .a(I_Imm_Funct3), .b(3'b001), .eq(comparator_11_eq), .lt(comparator_11_eq));  // open: gt
  Comparator #(.width(3)) comparator_12 (.a(I_Imm_Funct3), .b(3'b001), .eq(comparator_11_eq));  // open: gt, lt
  Comparator #(.width(3)) comparator_13 (
    .a(I_Imm_Funct3), .b(3'b001), .gt(comparator_11_eq), .eq(comparator_11_eq), .lt(comparator_11_eq));
  Comparator #(.width(7)) comparator_14 (
    .a(Instruction[6:0]), .b(7'b0000011), .eq(comparator_14_eq), .lt(comparator_14_lt));  // open: gt
  Comparator #(.width(7)) comparator_15 (.a(Instruction[6:0]), .b(7'b0000011), .eq(comparator_14_lt));  // open: gt, lt
  Comparator #(.width(7)) comparator_16 (
    .a(Instruction[6:0]), .b(7'b0000011), .gt(comparator_14_eq), .eq(comparator_14_lt));  // open: lt
  Comparator #(.width(3)) comparator_17 (
    .a(I_Imm_Funct3), .b(3'b010), .eq(comparator_17_eq), .lt(comparator_17_eq));  // open: gt
  Comparator #(.width(3)) comparator_18 (.a(I_Imm_Funct3), .b(3'b010), .eq(comparator_17_eq));  // open: gt, lt
  Comparator #(.width(3)) comparator_19 (
    .a(I_Imm_Funct3), .b(3'b010), .gt(comparator_17_eq), .eq(comparator_17_eq), .lt(comparator_17_eq));
  Comparator #(.width(7)) comparator_20 (
    .a(Instruction[6:0]), .b(7'b0000011), .eq(comparator_20_eq), .lt(comparator_20_lt));  // open: gt
  Comparator #(.width(7)) comparator_21 (.a(Instruction[6:0]), .b(7'b0000011), .eq(comparator_20_lt));  // open: gt, lt
  Comparator #(.width(7)) comparator_22 (
    .a(Instruction[6:0]), .b(7'b0000011), .gt(comparator_20_eq), .eq(comparator_20_lt));  // open: lt
  and and_4 (Is_lb, comparator_5_eq, comparator_8_eq);
  and and_5 (Is_lb, comparator_5_eq, comparator_8_lt);
  and and_6 (Is_lb, comparator_5_eq, comparator_8_lt);
  and and_7 (Is_lh, comparator_11_eq, comparator_14_eq);
  and and_8 (Is_lh, comparator_11_eq, comparator_14_lt);
  and and_9 (Is_lh, comparator_11_eq, comparator_14_lt);
  and and_10 (Is_lw, comparator_17_eq, comparator_20_eq);
  and and_11 (Is_lw, comparator_17_eq, comparator_20_lt);
  and and_12 (Is_lw, comparator_17_eq, comparator_20_lt);
  assign ByteFromMemData = {{24{multiplexer_1_out[7]}}, multiplexer_1_out};  // Bit_Extender bit_extender_1
  Multiplexer #(.select(2), .width(8)) multiplexer_1 (
    .in0(DataFromMem[7:0]), .in1(DataFromMem[15:8]), .in2(DataFromMem[23:16]), .in3(DataFromMem[31:24]),
    .out(multiplexer_1_out), .sel(MemAddress[1:0]));
  assign HalfWordFromMemData = {{16{multiplexer_2_out[15]}}, multiplexer_2_out};  // Bit_Extender bit_extender_2
  Multiplexer #(.select(2), .width(16)) multiplexer_2 (
    .in0(DataFromMem[15:0]), .in1(DataFromMem[23:8]), .in2(DataFromMem[31:16]), .out(multiplexer_2_out),
    .sel(MemAddress[1:0]));  // open: in3
  Multiplexer #(.width(32)) multiplexer_3 (.in1(ByteFromMemData), .out(DataToReg), .sel(isLb));  // open: in0
  Multiplexer #(.width(32)) multiplexer_4 (.in1(HalfWordFromMemData), .out(DataToReg), .sel(isLh));  // open: in0
  Multiplexer #(.width(32)) multiplexer_5 (.in1(DataFromMem), .out(DataToReg), .sel(isLw));  // open: in0

  // Other names for the same wires on the sheet: Opcode[6:0] = Instruction[6:0]; Funct3[2:0] = Instruction[14:12];
  //   ReadIndex[1:0] = MemAddress[1:0]

  // Notes on the sheet:
  //   INPUTS to your circuit
  //   DON'T CHANGE THE LOCATIONS OF THE INPUTS AND OUTPUTS!
  //   OUTPUT from your circuit
endmodule
