// Logisim project partial-store.circ as structural Verilog: 1 circuit, main circuit partial_store
module partial_store (
  input  [31:0] Instruction,
  input  [31:0] MemAddress,
  input  [31:0] DataFromReg,
  input  MemWEn,
  output [3:0] MemWriteMask,
  output [31:0] DataToMem
);

  wire isSb, isSh, isStoreInst, isSw, shouldWriteToMem;
  wire [3:0] ByteMemWriteMask, HalfWordMemWriteMask, multiplexer_4_out, WordMemWriteMask;
  wire [31:0] ByteDataToMem, HalfWordDataToMem, WordDataToMem;

  Comparator #(.mode("unsigned"), .width(7)) comparator_1 (
    .a(7'b0100011), .b(Instruction[6:0]), .eq(isStoreInst));  // open: gt, lt
  Comparator #(.mode("unsigned"), .width(3)) comparator_2 (
    .a(3'b000), .b(Instruction[14:12]), .eq(isSb));  // open: gt, lt
  Comparator #(.mode("unsigned"), .width(3)) comparator_3 (
    .a(3'b001), .b(Instruction[14:12]), .eq(isSh));  // open: gt, lt
  Comparator #(.mode("unsigned"), .width(3)) comparator_4 (
    .a(3'b010), .b(Instruction[14:12]), .eq(isSw));  // open: gt, lt
  Multiplexer #(.select(2), .width(4)) multiplexer_1 (
    .in0(4'b0001), .in1(4'b0010), .in2(4'b0100), .in3(4'b1000), .out(ByteMemWriteMask), .sel(MemAddress[1:0]));
  Multiplexer #(.select(2), .width(4)) multiplexer_2 (
    .in0(4'b0011), .in2(4'b1100), .out(HalfWordMemWriteMask), .sel(MemAddress[1:0]));  // open: in1, in3
  Multiplexer #(.width(4)) multiplexer_3 (.in1(4'b1111), .out(WordMemWriteMask), .sel(isSw));  // open: in0
  Multiplexer #(.select(3), .width(4)) multiplexer_4 (
    .in0(ByteMemWriteMask), .in1(HalfWordMemWriteMask), .in2(WordMemWriteMask), .out(multiplexer_4_out),
    .sel(Instruction[14:12]));  // open: in3, in4, in5, in6, in7
  Multiplexer #(.select(2), .width(32)) multiplexer_5 (
    .in0({{24{1'b0}}, DataFromReg[7:0]}), .in1({{16{1'b0}}, DataFromReg[7:0], {8{1'b0}}}),
    .in2({{8{1'b0}}, DataFromReg[7:0], {16{1'b0}}}), .in3({DataFromReg[7:0], {24{1'b0}}}),
    .out(ByteDataToMem), .sel(MemAddress[1:0]));
  Multiplexer #(.select(2), .width(32)) multiplexer_6 (
    .in0({{16{1'b0}}, DataFromReg[15:0]}), .in2({DataFromReg[15:0], {16{1'b0}}}), .out(HalfWordDataToMem),
    .sel(MemAddress[1:0]));  // open: in1, in3
  Multiplexer #(.width(32)) multiplexer_7 (.in1(DataFromReg), .out(WordDataToMem), .sel(isSw));  // open: in0
  Multiplexer #(.width(4)) multiplexer_8 (
    .in0(4'b0000), .in1(multiplexer_4_out), .out(MemWriteMask), .sel(shouldWriteToMem));
  and and_1 (shouldWriteToMem, MemWEn, isStoreInst);
  Multiplexer #(.select(3), .width(32)) multiplexer_9 (
    .in0(ByteDataToMem), .in1(HalfWordDataToMem), .in2(WordDataToMem), .out(DataToMem),
    .sel(Instruction[14:12]));  // open: in3, in4, in5, in6, in7

  // Other names for the same wires on the sheet: ByteFromReg[7:0] = DataFromReg[7:0];
  //   ByteIdxOne[15:8] = DataFromReg[7:0]; ByteIdxThree[31:24] = DataFromReg[7:0];
  //   ByteIdxTwo[23:16] = DataFromReg[7:0]; ByteIdxZero[7:0] = DataFromReg[7:0];
  //   HalfWordFromReg[15:0] = DataFromReg[15:0]; HalfWordIdxOne[31:16] = DataFromReg[15:0];
  //   HalfWordIdxZero[15:0] = DataFromReg[15:0]; Opcode[6:0] = Instruction[6:0]; Funct3[2:0] = Instruction[14:12];
  //   StartIdx[1:0] = MemAddress[1:0]

  // Notes on the sheet:
  //   INPUTS to your circuit
  //   DON'T CHANGE THE LOCATIONS OF THE INPUTS AND OUTPUTS!
  //   OUTPUT from your circuit
endmodule
